# Fritzing sketch electronics-diagram (saved by Fritzing 0.8.7b)
breadboards: 1

parts:
  Raspberry_Pi_1 = Raspberry Pi 3
  MD09B1 = A4988 Stepper Motor Driver Carrier  # not connected
  J1 = Power Jack [package=power_jack_slot]
  M1 = Stepper Motor - Bipolar  # not connected

nets:
  3V3: Raspberry_Pi_1.3v3, Raspberry_Pi_1.3V3
  GND: Raspberry_Pi_1.GND, J1.GND

notes:
  5 inch LCD Display
  Connects via 26 GPIO ports
  5V jumper goes to breadboard
